# Fritzing sketch ESP32_Balancing_Robot_Pinout (saved by Fritzing 1.0.6)

parts:
  Part1 = InvenSense MPU6050
  VCC1 = Battery [internal_resistance=0.1Ω]  # not connected
  A1 = ESP32-S3 supermini  # not connected
  DC_Mot_Enc1 = DC Motor with two-phase hall-encoder [part_number=VT-E-G25A-06-177E]
  DC_Mot_Enc2 = DC Motor with two-phase hall-encoder [part_number=VT-E-G25A-06-177E]  # not connected
  Part2 = Motor Driver 1A Dual TB6612FNG  # not connected

nets:
  N1: Part1.GND, DC_Mot_Enc1.pin2

custom parts:
  ESP32-S3 supermini: Esp32-S3 Development board ESP32 SuperMini development board ESP32 Development board WiFi Bluetooth.
